# Fritzing sketch Circuito completo (saved by Fritzing 0.9.3b)
breadboards: 1

parts:
  Arduino1_Slave = Arduino Uno (Rev3)
  Display_LCD = LCD screen
  R1 = Resistor [tolerance=±5% resistance=2.2k package=THT]
  Bluetooth_HC-06 = Bluetooth HC-05 Macho
  RTC_DS3232 = Real Time Clock Module - DS1307 RTC Breakout Board
  M1 = Stepper Motor - Bipolar
  Arduino1_Master = Arduino Uno (Rev3)
  KEYPAD1 = Membrane Matrix Keypad

nets:
  N1: Arduino1_Slave.A4/SDA, RTC_DS3232.SDA
  N2: Arduino1_Slave.A5/SCL, RTC_DS3232.SCL
  N3: Arduino1_Slave.D10_PWM/SS, M1.D
  N4: Arduino1_Slave.D11_PWM/MOSI, M1.B
  N5: Arduino1_Slave.D12/MISO, M1.C
  N6: Arduino1_Slave.D13/SCK, M1.A
  N7: Arduino1_Slave.D2, Display_LCD.RS
  N8: Arduino1_Slave.D3_PWM, Display_LCD.E
  N9: Arduino1_Slave.D4, Display_LCD.DB4
  N10: Arduino1_Slave.D5_PWM, Display_LCD.DB5
  N11: Arduino1_Slave.D6_PWM, Display_LCD.DB6
  N12: Arduino1_Slave.D7, Display_LCD.DB7
  5V: Arduino1_Slave.5V, Display_LCD.VDD, Bluetooth_HC-06.VCC, RTC_DS3232.5V
  GND: Arduino1_Slave.GND, Display_LCD.VSS, Display_LCD.R/W, R1.Pin_0, Bluetooth_HC-06.GND, RTC_DS3232.GND
  N13: Display_LCD.V0, R1.Pin_1
  N14: Bluetooth_HC-06.TXD, Arduino1_Master.D2
  N15: Bluetooth_HC-06.RXD, Arduino1_Master.D3_PWM
  N16: Arduino1_Master.D8, KEYPAD1.5
  N17: Arduino1_Master.D9_PWM, KEYPAD1.6
  N18: Arduino1_Master.D10_PWM/SS, KEYPAD1.7
  N19: Arduino1_Master.D4, KEYPAD1.1
  N20: Arduino1_Master.D5_PWM, KEYPAD1.2
  N21: Arduino1_Master.D6_PWM, KEYPAD1.3
  N22: Arduino1_Master.D7, KEYPAD1.4

custom parts:
  Membrane Matrix Keypad: Membrane Matrix 3x4 Keypad
