# Fritzing sketch HC-06 (saved by Fritzing 0.9.3b)

parts:
  Componente1 = Bluetooth HC-05 Macho
  Componente2 = Arduino Uno (Rev3)

nets:
  N1: Componente1.TXD, Componente2.D3_PWM
  N2: Componente1.RXD, Componente2.D2
  VCC: Componente1.VCC, Componente2.5V
  GND: Componente1.GND, Componente2.GND
