# Fritzing sketch RTC DS3232 (saved by Fritzing 0.9.3b)

parts:
  Componente1 = Real Time Clock Module - DS1307 RTC Breakout Board
  Componente2 = Arduino Uno (Rev3)

nets:
  5V: Componente1.5V, Componente2.5V
  GND: Componente1.GND, Componente2.GND
  N1: Componente1.SCL, Componente2.A5/SCL
  N2: Componente1.SDA, Componente2.A4/SDA
